# Fritzing sketch humidity_fan (saved by Fritzing 0.9.3b)
breadboards: 1

parts:
  Part1 = Adafruit Trinket 5V
  AM1 = AM2302 Humidity and Temperature Sensor
  R1 = Resistor [tolerance=±5% resistance=10k package="2512 [SMD]"]
  F1 = Fan - Ventilador [package=THT]

nets:
  GND: Part1.GND, AM1.GND, F1.GND
  N1: Part1.#2, AM1.DATA, R1.Pin_0
  N2: Part1.#3, F1.5V
  +5V: Part1.+5V, AM1.VDD, R1.Pin_1

custom parts:
  Adafruit Trinket 5V: Trinket may be small, but do not be fooled by its size! It's a tiny microcontroller board, built around the Atmel ATtiny85, a little chip with a lot of power. We wanted to design a microcontroller board that was small enough to fit into any project, and low cost enough to use without hesitation. Perfect for when you don't want to give up your expensive dev-board and you aren't willing to take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
  Fan - Ventilador: Ventilador de 2 pines, se encuentra comunmente en computadoras de escritorio
